# Fritzing sketch sparky_layer_counter_deluxe (saved by Fritzing 0.9.3b)
breadboards: 1

parts:
  Part1 = Arduino Nano (Rev3.0)
  U1 = LCD-16X2 [package=lcd-16x2]
  S1 = Pushbutton [package="[SMD]"]
  U2 = TRANSISTOR_NPN_2 [part_number=2N3904 package=to-92]
  R1 = Resistor [tolerance=±5% resistance=10k package=THT]
  R2 = Trimmer Potentiometer [maximum_resistance=10kΩ package=THT]
  S2 = Pushbutton [package="[SMD]"]
  Q2 = LTR-301 [package=ltr-301]
  R3 = Resistor [tolerance=±5% resistance=4.7k package=THT]

nets (from the breadboard view):
  GND: Part1.GND, U1.VSS, U1.R_W, U1.K, S1.Pin_3, S1.Pin_4, R2.leg1, S2.Pin_3, S2.Pin_4, Q2.E
  N1: Part1.D2, U1.DB7
  N2: Part1.D3, U1.DB6
  N3: Part1.D4, U1.DB5
  N4: Part1.D5, U1.DB4
  N5: Part1.D7, S2.Pin_1, S2.Pin_2
  N6: Part1.D8, S1.Pin_1, S1.Pin_2
  N7: Part1.D11/MOSI, U1.E
  N8: Part1.D12/MISO, U1.RS
  5V: Part1.5V, U1.VDD, U2.C, R1.Pin_0, R2.leg2
  N9: Part1.A2, R3.Pin_0
  N10: Part1.A0, R1.Pin_1, Q2.C
  N11: U1.VO, R2.wiper
  N12: U1.A, U2.E
  N13: U2.B, R3.Pin_1

custom parts:
  LTR-301: Through-hole side-receiving IR phototransistor
